# Fritzing sketch antaDomotica (saved by Fritzing 0.9.6b)
breadboards: 2

parts:
  U1 = NodeMCU V1.0
  HC-SR04_Sensor_1 = HC-SR04 Ultrasonic Distance Sensor
  HC-SR04_Sensor_2 = HC-SR04 Ultrasonic Distance Sensor
  SM1 = 28BYJ-48 Stepper Motor [part_number=28BYJ-48]
  Driver1 = 28BYJ-48 Driver Module [part_number=ULN2003 package=THT]
  Mod1 = YL-99 Limit switch and LED
  Mod2 = YL-99 Limit switch and LED
  Mod3 = KY-018 Photoresistor Module [package="Breakout board"]
  S1 = Pushbutton [package="[THT]"]
  S2 = Pushbutton [package="[THT]"]
  S3 = Pushbutton [package="[THT]"]
  YwRobot_Power_Supply1 = YwRobot Breadboard Power Supply [part_number=545043]
  R1 = Resistor [tolerance=±5% resistance=4.7 package="0603 [SMD]"]
  R2 = Resistor [tolerance=±5% resistance=4.7 package="0603 [SMD]"]
  R3 = Resistor [tolerance=±5% resistance=4.7 package="0603 [SMD]"]
  U2 = NodeMCU V1.0
  DHT1 = DHT11 Humitidy and Temperature Sensor

nets:
  N1: U1.D0, S3.Pin_1, S3.Pin_2, R2.Pin_0
  N2: U1.D1, Driver1.IN1
  N3: U1.D2, Driver1.IN2
  N4: U1.D3, S1.Pin_1, S1.Pin_2, R1.Pin_0
  N5: U1.D4, S2.Pin_1, S2.Pin_2, R3.Pin_0
  N6: U1.D5, Driver1.IN3
  N7: U1.D6, Driver1.IN4
  N8: U1.D7, Mod1.OUT
  GND: U1.GND, HC-SR04_Sensor_1.GND, HC-SR04_Sensor_2.GND, Driver1.GND, Mod3.-, YwRobot_Power_Supply1.GND#11, U2.GND, DHT1.NULL
  3V3: U1.3V3, Mod3.Vin
  VIN: U1.Vin, HC-SR04_Sensor_1.VCC, HC-SR04_Sensor_2.VCC, Driver1.Vmotor, YwRobot_Power_Supply1.VCC#5, U2.Vin
  N9: U1.A0, Mod3.S
  N10: HC-SR04_Sensor_1.TRIG, U2.D6
  N11: HC-SR04_Sensor_1.ECHO, U2.D1
  N12: HC-SR04_Sensor_2.TRIG, U2.D2
  N13: HC-SR04_Sensor_2.ECHO, U2.D5
  N14: SM1.blue-pin, Driver1.blue-pin
  N15: SM1.pink-pin, Driver1.pink-pin
  N16: SM1.yellow-pin, Driver1.yellow-pin
  N17: SM1.orange-pin, Driver1.orange-pin
  N18: SM1.red-pin, Driver1.red-pin
  N19: Mod1.VCC, Mod2.OUT
  GND_2: Mod1.GND, Mod2.GND, S1.Pin_3, S1.Pin_4, S2.Pin_3, S2.Pin_4, S3.Pin_3, S3.Pin_4, YwRobot_Power_Supply1.GND#13
  N20: Mod2.VCC, U2.D0
  N21: YwRobot_Power_Supply1.VCC#9, R1.Pin_1, R2.Pin_1, R3.Pin_1
  N22: U2.D7, DHT1.GND
  N23: U2.3V3, DHT1.DATA

custom parts:
  NodeMCU V1.0: ESP8266 based NodeMCU
  28BYJ-48 Stepper Motor: Unipolar Stepper Motor 28BYJ-48 Top coil - pink & orange Bottom coil - blue & yellow Common rail - red Connector pins: blue - pink - yellow - orange - red
  28BYJ-48 Driver Module: ULN2003 Driver Module for the 28BYJ-48 Unipolar Stepper Motor LED A - Blue wire - Bottom coil left LED B - Pink wire - Top coil left LED C - Yellow wire - Bottom coil right LED D - Orange wire - Top coil right Common rail - red Connector pins: blue - pink - yellow - orange - red Control pins - IN1 to IN4 Power pins - GND & Vmotor (5-12V) On/Off jumper (if removed, power to motor is cut).
  KY-018 Photoresistor Module: KY-018 Photoresistor module, used to measure light intensity. It can determine the presence or absence of light.
  YwRobot Breadboard Power Supply: The YwRobot Breadboard Power Supply (MB-V2) has two power rails; they can be 5V or 3V3. Power to the module can be provided through the female USB socket or through the A10 (female) 2.1mm power jack.
  DHT11 Humitidy and Temperature Sensor: DHT11 Humidity and Temperature Sensor
